// Logisim project New CPU version to impress.circ as structural Verilog: 1 circuit, main circuit main
module main (
  input  load,
  input  [3:0] B,
  input  in_3,
  input  in_4,
  input  in_5,
  output [3:0] out_6,
  output [3:0] out_7,
  output [3:0] out_8
);

  wire adder_2_cout, clock_1_out, clock_2_out, clock_3_out, clock_4_out;
  wire [3:0] adder_1_out, adder_2_out, and_1_out, multiplexer_1_out, multiplexer_2_out, or_1_out,
       Ram_Buffer_q, rom_1_data, undriven;

  Clock clock_1 (.out(clock_1_out));
  Hex_Digit_Display hex_digit_display_1 (.value(out_7));  // open: dp
  Register #(.width(4)) register_1 (.D(adder_1_out), .Q(out_7), .clk(clock_1_out));  // open: en, clr
  Adder #(.width(4)) adder_1 (.a(out_7), .b(4'b0001), .out(adder_1_out));  // open: cin, cout
  ROM #(.addrWidth(4), .dataWidth(4)) rom_1 (.addr(out_7), .data(rom_1_data), .sel(1'b1));
  Hex_Digit_Display hex_digit_display_2 (.value(rom_1_data));  // open: dp
  Clock clock_2 (.out(clock_2_out));
  RAM #(.addrWidth(4), .dataWidth(4)) ram_1 (
    .addr(out_7), .data(out_6), .clk(clock_2_out), .ld(in_5));  // open: sel, clr
  Clock clock_3 (.out(clock_3_out));
  Adder #(.width(4)) adder_2 (.a(out_6), .b(multiplexer_2_out), .out(adder_2_out), .cout(adder_2_cout));  // open: cin
  assign and_1_out = out_6 & multiplexer_2_out;  // AND_Gate and_1, 4 bits wide
  assign or_1_out = out_6 | multiplexer_2_out;  // OR_Gate or_1, 4 bits wide
  Register #(.width(4)) Ram_Buffer (.D(out_6), .en(in_4), .Q(Ram_Buffer_q), .clk(clock_3_out));  // open: clr
  Multiplexer #(.select(2), .width(4)) multiplexer_1 (
    .in0(adder_2_out), .in1(and_1_out), .in2(or_1_out), .in3(undriven), .out(multiplexer_1_out),
    .sel(rom_1_data[1:0]));  // open: en
  Multiplexer #(.width(4)) multiplexer_2 (
    .in0(B), .in1(Ram_Buffer_q), .out(multiplexer_2_out), .sel(in_3));  // open: en
  Hex_Digit_Display hex_digit_display_3 (.value(multiplexer_2_out));  // open: dp
  Register #(.width(4)) register_2 (.D(multiplexer_1_out), .en(load), .Q(out_6), .clk(clock_4_out));  // open: clr
  Clock clock_4 (.out(clock_4_out));
  Hex_Digit_Display hex_digit_display_4 (.value(out_6));  // open: dp

  assign out_8 = out_6;

  // Notes on the sheet:
  //   PC Display
  //   PC(Program Control)
  //   Instruction Memory (ROM)
  //   contents of rom_1 (hex, n*v repeats v):
  //   0 1 2 3 0 1 2 3 0 1 2 3 0 1 2 3
  //   Rom Display
  //   ALU Control Unit
  //   CPU State Register
  //   Mux Result
  //   Result
endmodule
